# Fritzing sketch tubes_sisin (saved by Fritzing 0.9.3b)
breadboards: 1

parts:
  Part1 = Arduino Uno (Rev3)
  T1 = LM35 Temperature Sensor [package="TO92 [THT]"]
  Part2 = LCD1602-I2C
  LED1 = LEDs [package=led10mm]
  LED2 = LEDs [package=led10mm]
  U1 = SWITCH-SPST-2 [package=switch-spst-vertical]
  VCC1 = Battery block 9V

nets:
  N1: Part1.A0, T1.Vout
  N2: Part1.A4/SDA, Part2.SDA
  N3: Part1.A5/SCL, Part2.SCL
  N4: Part1.D10_PWM/SS, LED2.A
  N5: Part1.D11_PWM/MOSI, LED1.A
  N6: Part1.GND, LED1.C, LED2.C
  N7: Part1.VIN, U1.P
  N8: T1.+Vs, Part2.VCC, VCC1.-
  GND: T1.GND, Part2.GND
  N9: U1.O, VCC1.+

custom parts:
  LCD1602-I2C: A standard character display, usually with 2x16 characters. Comes in many colors with LCM1602 IIC attached.
